# Fritzing sketch robotikaProjekt (saved by Fritzing 0.9.10b)
breadboards: 1

parts:
  Part1 = Arduino Micro (Rev3)
  PIR1 = PIR sensor
  J1 = Piezo Speaker
  R1 = Resistor [tolerance=±5% resistance=220 package="0603 [SMD]"]
  LED1 = LED - 5mm [color="Red (633nm)" current=0.030 package="5 mm [THT]"]
  LED2 = LED - 5mm [color="Green (570nm)" current=0.030 package="5 mm [THT]"]
  R2 = Resistor [tolerance=±5% resistance=220 package="1206 [SMD]"]
  Part2 = LCD1602-I2C
  S1 = Pushbutton [package="[THT]"]
  S2 = Pushbutton [package="[THT]"]
  S3 = Pushbutton [package="[THT]"]
  S4 = Pushbutton [package="[THT]"]
  R3 = Resistor [tolerance=±5% resistance=10k package="0805 [SMD]"]
  R4 = Resistor [tolerance=±5% resistance=10k package="0805 [SMD]"]
  R5 = Resistor [tolerance=±5% resistance=10k package="0805 [SMD]"]
  R6 = Resistor [tolerance=±5% resistance=10k package="0805 [SMD]"]

nets:
  GND: Part1.GND, PIR1.GND, J1.pin1, LED1.cathode, LED2.cathode, Part2.GND, R3.Pin_1, R4.Pin_1, R5.Pin_1, R6.Pin_1
  N1: Part1.D2/SDA, Part2.SDA
  N2: Part1.D3/SCL, Part2.SCL
  N3: Part1.D9_PWM/A9, R1.Pin_0
  N4: Part1.D10_PWM/A10, R2.Pin_0
  N5: Part1.D11_PWM, J1.pin2
  N6: Part1.D12_PWM/A11, PIR1.SIG
  5V: Part1.5V, PIR1.VDD, Part2.VCC, S1.Pin_3, S1.Pin_4, S2.Pin_3, S2.Pin_4, S3.Pin_3, S3.Pin_4, S4.Pin_3, S4.Pin_4
  N7: Part1.A3, S4.Pin_1, S4.Pin_2, R6.Pin_0
  N8: Part1.A2, S3.Pin_1, S3.Pin_2, R5.Pin_0
  N9: Part1.A1, S2.Pin_1, S2.Pin_2, R4.Pin_0
  N10: Part1.A0, S1.Pin_1, S1.Pin_2, R3.Pin_0
  N11: R1.Pin_1, LED1.anode
  N12: LED2.anode, R2.Pin_1

custom parts:
  LCD1602-I2C: A standard character display, usually with 2x16 characters. Comes in many colors with LCM1602 IIC attached.
